// Logisim project projet_Processeur.circ as structural Verilog: 15 circuits, main circuit main
module main (
  input  [7:0] A,
  input  [7:0] B,
  input  [1:0] ope,
  input  [1:0] in_4,
  output [7:0] res,
  output overflow
);

  wire bloccomparaisons_1_res;
  wire [7:0] bit_extender_1_out, blocarithmetiques_1_res, bloclogiques_1_res;

  BlocArithmetiques blocarithmetiques_1 (
    .A(A), .B(B), .ope(ope[0]), .res(blocarithmetiques_1_res), .overflow(overflow));
  BlocLogiques bloclogiques_1 (.B(B), .ope(ope), .res(bloclogiques_1_res));  // open: A
  assign bit_extender_1_out = {{7{bloccomparaisons_1_res}}, bloccomparaisons_1_res};  // Bit_Extender bit_extender_1
  BlocComparaisons bloccomparaisons_1 (.A(A), .B(B), .ope(ope), .res(bloccomparaisons_1_res));
  Multiplexer #(.select(2), .width(8)) multiplexer_1 (
    .in0(blocarithmetiques_1_res), .in1(bloclogiques_1_res), .in2(bit_extender_1_out), .in3({8{1'b0}}),
    .out(res), .sel(in_4));
  // also tied to GND on the sheet: ope[1]
endmodule

module add1bit (
  input  A,
  input  B,
  input  R,
  output res,
  output res_R
);

  wire and_1_out, and_2_out, and_3_out, or_1_out, xor_1_out;

  xor xor_1 (xor_1_out, A, B);
  and and_1 (and_1_out, A, B);
  and and_2 (and_2_out, R, A);
  and and_3 (and_3_out, R, B);
  xor xor_2 (res, xor_1_out, R);
  or or_1 (or_1_out, and_2_out, and_3_out);
  or or_2 (res_R, and_1_out, or_1_out);
endmodule

module add (
  input  [7:0] A,
  input  [7:0] B,
  output [7:0] res,
  output overflow
);

  wire add1bit_1_res_r, add1bit_2_res_r, add1bit_3_res_r, add1bit_4_res_r, add1bit_5_res_r, add1bit_6_res_r,
       add1bit_7_res_r;

  add1bit add1bit_1 (.A(A[0]), .B(B[0]), .R(1'b0), .res(res[0]), .res_R(add1bit_1_res_r));
  add1bit add1bit_2 (.A(A[1]), .B(B[1]), .R(add1bit_1_res_r), .res(res[1]), .res_R(add1bit_2_res_r));
  add1bit add1bit_3 (.A(A[2]), .B(B[2]), .R(add1bit_2_res_r), .res(res[2]), .res_R(add1bit_3_res_r));
  add1bit add1bit_4 (.A(A[3]), .B(B[3]), .R(add1bit_3_res_r), .res(res[3]), .res_R(add1bit_4_res_r));
  add1bit add1bit_5 (.A(A[4]), .B(B[4]), .R(add1bit_4_res_r), .res(res[4]), .res_R(add1bit_5_res_r));
  add1bit add1bit_6 (.A(A[5]), .B(B[5]), .R(add1bit_5_res_r), .res(res[5]), .res_R(add1bit_6_res_r));
  add1bit add1bit_7 (.A(A[6]), .B(B[6]), .R(add1bit_6_res_r), .res(res[6]), .res_R(add1bit_7_res_r));
  add1bit add1bit_8 (.A(A[7]), .B(B[7]), .R(add1bit_7_res_r), .res(res[7]), .res_R(overflow));
endmodule

module sub (
  input  [7:0] A,
  input  [7:0] B,
  output [7:0] res
);

  wire add_1_overflow, add_2_overflow;
  wire [7:0] add_1_res, not_1_out;

  assign not_1_out = ~B;  // NOT_Gate not_1, 8 bits wide
  add add_1 (.A(not_1_out), .B(8'h1), .res(add_1_res), .overflow(add_1_overflow));
  add add_2 (.A(A), .B(add_1_res), .res(res), .overflow(add_2_overflow));
  // also tied to GND on the sheet: {add_1_overflow, add_2_overflow}
endmodule

module and8bit (
  input  [7:0] B,
  input  [7:0] A,
  output [7:0] res
);

  assign res = B & A;  // AND_Gate and_1, 8 bits wide
endmodule

module or8bit (
  input  [7:0] B,
  input  [7:0] A,
  output [7:0] res
);

  assign res = B | A;  // OR_Gate or_1, 8 bits wide
endmodule

module xor8bit (
  input  [7:0] B,
  input  [7:0] A,
  output [7:0] res
);

  assign res = B ^ A;  // XOR_Gate xor_1, 8 bits wide
endmodule

module Equal (
  input  [7:0] B,
  input  [7:0] A,
  output res
);

  wire and_1_out, and_2_out, and_3_out, and_4_out, and_5_out, and_6_out;
  wire [7:0] not_1_out, xor_1_out;

  assign xor_1_out = B ^ A;  // XOR_Gate xor_1, 8 bits wide
  assign not_1_out = ~xor_1_out;  // NOT_Gate not_1, 8 bits wide
  and and_1 (and_1_out, not_1_out[0], not_1_out[1]);
  and and_2 (and_2_out, and_1_out, not_1_out[2]);
  and and_3 (and_3_out, and_2_out, not_1_out[3]);
  and and_4 (and_4_out, and_3_out, not_1_out[4]);
  and and_5 (and_5_out, and_4_out, not_1_out[5]);
  and and_6 (and_6_out, and_5_out, not_1_out[6]);
  and and_7 (res, and_6_out, not_1_out[7]);
endmodule

module diff (
  input  [7:0] B,
  input  [7:0] A,
  output res
);

  wire equal_1_res;

  Equal equal_1 (.B(B), .A(A), .res(equal_1_res));
  not not_1 (res, equal_1_res);
endmodule

module inf (
  input  [7:0] A,
  input  [7:0] B,
  output res
);

  wire or_1_out, or_2_out, or_3_out, or_4_out, or_5_out, or_6_out;
  wire [7:0] and_1_out, not_1_out;

  assign not_1_out = ~A;  // NOT_Gate not_1, 8 bits wide
  assign and_1_out = not_1_out & B;  // AND_Gate and_1, 8 bits wide
  or or_1 (or_1_out, and_1_out[0], and_1_out[1]);
  or or_2 (or_2_out, or_1_out, and_1_out[2]);
  or or_3 (or_3_out, or_2_out, and_1_out[3]);
  or or_4 (or_4_out, or_3_out, and_1_out[4]);
  or or_5 (or_5_out, or_4_out, and_1_out[5]);
  or or_6 (or_6_out, or_5_out, and_1_out[6]);
  or or_7 (res, or_6_out, and_1_out[7]);
endmodule

module sup (
  input  [7:0] A,
  input  [7:0] B,
  output res
);

  wire inf_1_res;

  not not_1 (res, inf_1_res);
  inf inf_1 (.A(A), .B(B), .res(inf_1_res));
endmodule

module LSL (
  input  [7:0] A,
  output [7:0] res
);


  assign res = {A[6:0], 1'b0};
endmodule

module BlocArithmetiques (
  input  [7:0] A,
  input  [7:0] B,
  input  ope,
  output [7:0] res,
  output overflow
);

  wire add_1_overflow;
  wire [7:0] add_1_res, sub_1_res;

  add add_1 (.A(A), .B(B), .res(add_1_res), .overflow(add_1_overflow));
  sub sub_1 (.A(A), .B(B), .res(sub_1_res));
  Multiplexer #(.width(8)) multiplexer_1 (.in0(add_1_res), .in1(sub_1_res), .out(res), .sel(ope));
  Multiplexer multiplexer_2 (.in0(add_1_overflow), .in1(1'b0), .out(overflow), .sel(ope));
endmodule

module BlocLogiques (
  input  [7:0] A,
  input  [7:0] B,
  input  [1:0] ope,
  output [7:0] res
);

  wire [7:0] and8bit_1_res, lsl_1_res, or8bit_1_res, xor8bit_1_res;

  and8bit and8bit_1 (.B(B), .A(A), .res(and8bit_1_res));
  or8bit or8bit_1 (.B(B), .A(A), .res(or8bit_1_res));
  xor8bit xor8bit_1 (.B(B), .A(A), .res(xor8bit_1_res));
  LSL lsl_1 (.A(A), .res(lsl_1_res));
  Multiplexer #(.select(2), .width(8)) multiplexer_1 (
    .in0(and8bit_1_res), .in1(or8bit_1_res), .in2(xor8bit_1_res), .in3(lsl_1_res), .out(res), .sel(ope));
endmodule

module BlocComparaisons (
  input  [7:0] A,
  input  [7:0] B,
  input  [1:0] ope,
  output res
);

  wire diff_1_res, equal_1_res, inf_1_res, sup_1_res;

  Equal equal_1 (.B(A), .A(B), .res(equal_1_res));
  diff diff_1 (.B(A), .A(B), .res(diff_1_res));
  inf inf_1 (.A(A), .B(B), .res(inf_1_res));
  sup sup_1 (.A(A), .B(B), .res(sup_1_res));
  Multiplexer #(.select(2)) multiplexer_1 (
    .in0(equal_1_res), .in1(diff_1_res), .in2(inf_1_res), .in3(sup_1_res), .out(res), .sel(ope));
endmodule
